// Digital circuit inst-mem-v2.dig as structural Verilog
module inst_mem_v2 (
  input  [7:0] ADDR,
  input  [4:0] PROG,
  output [31:0] IW
);

  wire [31:0] _00, _01, _02, _03, _04, _05, _06, _07, _08, _09, _10, _11, _12, _13, _14, _15, _16, _17, _18,
       _19;

  ROM #(.AddrBits(8), .Bits(32)) _00_add_r (.A(ADDR), .sel(1'b1), .D(_00));
  ROM #(.AddrBits(8), .Bits(32)) _01_add_i (.A(ADDR), .sel(1'b1), .D(_01));
  ROM #(.AddrBits(8), .Bits(32)) _02_sll_r (.A(ADDR), .sel(1'b1), .D(_02));
  ROM #(.AddrBits(8), .Bits(32)) _03_sll_i (.A(ADDR), .sel(1'b1), .D(_03));
  ROM #(.AddrBits(8), .Bits(32)) _04_srl_r (.A(ADDR), .sel(1'b1), .D(_04));
  ROM #(.AddrBits(8), .Bits(32)) _05_srl_i (.A(ADDR), .sel(1'b1), .D(_05));
  ROM #(.AddrBits(8), .Bits(32)) _06_sd_ld (.A(ADDR), .sel(1'b1), .D(_06));
  ROM #(.AddrBits(8), .Bits(32)) _07_sw_lw (.A(ADDR), .sel(1'b1), .D(_07));
  ROM #(.AddrBits(8), .Bits(32)) _08_jal (.A(ADDR), .sel(1'b1), .D(_08));
  ROM #(.AddrBits(8), .Bits(32)) _09_j (.A(ADDR), .sel(1'b1), .D(_09));
  ROM #(.AddrBits(8), .Bits(32)) _10_beq (.A(ADDR), .sel(1'b1), .D(_10));
  ROM #(.AddrBits(8), .Bits(32)) _11_blt (.A(ADDR), .sel(1'b1), .D(_11));
  ROM #(.AddrBits(8), .Bits(32)) _12_bge (.A(ADDR), .sel(1'b1), .D(_12));
  ROM #(.AddrBits(8), .Bits(32)) _13_mul (.A(ADDR), .sel(1'b1), .D(_13));
  ROM #(.AddrBits(8), .Bits(32)) _14_lui (.A(ADDR), .sel(1'b1), .D(_14));
  ROM #(.AddrBits(8), .Bits(32)) _15_quadratic (.A(ADDR), .sel(1'b1), .D(_15));
  ROM #(.AddrBits(8), .Bits(32)) _16_get_bitseq (.A(ADDR), .sel(1'b1), .D(_16));
  ROM #(.AddrBits(8), .Bits(32)) _17_fib_rec (.A(ADDR), .sel(1'b1), .D(_17));
  ROM #(.AddrBits(8), .Bits(32)) rom_1 (.A(ADDR), .sel(1'b1), .D(_18));
  ROM #(.AddrBits(8), .Bits(32)) rom_2 (.A(ADDR), .sel(1'b1), .D(_19));
  Multiplexer #(.Selector_Bits(5), .Bits(32)) multiplexer_1 (
    .sel(PROG), .in_0(_00), .in_1(_01), .in_2(_02), .in_3(_03), .in_4(_04), .in_5(_05), .in_6(_06),
    .in_7(_07), .in_8(_08), .in_9(_09), .in_10(_10), .in_11(_11), .in_12(_12), .in_13(_13), .in_14(_14),
    .in_15(_15), .in_16(_16), .in_17(_17), .in_18(_18), .in_19(_19), .in_20({32{1'b0}}), .in_21({32{1'b0}}),
    .in_22({32{1'b0}}), .in_23({32{1'b0}}), .in_24({32{1'b0}}), .in_25({32{1'b0}}), .in_26({32{1'b0}}),
    .in_27({32{1'b0}}), .in_28({32{1'b0}}), .in_29({32{1'b0}}), .in_30({32{1'b0}}), .in_31({32{1'b0}}),
    .out(IW));

  // Notes on the sheet:
  //   contents of _00_add_r (hex, n*v repeats v):
  //   100513,200593,b50633,c0001073
  //   contents of _01_add_i (hex, n*v repeats v):
  //   100513,250613,c0001073
  //   contents of _02_sll_r (hex, n*v repeats v):
  //   100593,200613,c59533,c0001073
  //   contents of _03_sll_i (hex, n*v repeats v):
  //   100593,359513,c0001073
  //   contents of _04_srl_r (hex, n*v repeats v):
  //   800593,100613,c5d533,c0001073
  //   contents of _05_srl_i (hex, n*v repeats v):
  //   2000593,25d513,c0001073
  //   contents of _06_sd_ld (hex, n*v repeats v):
  //   8000113,ff810113,513,6300293,513023,13503,c0001073
  //   contents of _07_sw_lw (hex, n*v repeats v):
  //   8000113,ff810113,513,6300293,512023,12503,c0001073
  //   contents of _08_jal (hex, n*v repeats v):
  //   100513,200593,8000ef,c0001073,b50533,8067
  //   contents of _09_j (hex, n*v repeats v):
  //   100513,80006f,513,c0001073
  //   contents of _10_beq (hex, n*v repeats v):
  //   100513,100593,b50463,513,c0001073
  //   contents of _11_blt (hex, n*v repeats v):
  //   100513,200593,b54463,513,c0001073
  //   contents of _12_bge (hex, n*v repeats v):
  //   200513,100593,b55463,513,c0001073
  //   contents of _13_mul (hex, n*v repeats v):
  //   300513,300593,2b50533,c0001073
  //   contents of _14_lui (hex, n*v repeats v):
  //   1537,c0001073
  //   contents of _15_quadratic (hex, n*v repeats v):
  //   200513,300593,400613,500693,8000ef,c0001073,2a502b3,2b282b3,2c50333
  //   ,628533,d50533,8067
  //   contents of _16_get_bitseq (hex, n*v repeats v):
  //   17537,fa55051b,c00593,f00613,8000ef,c0001073,40b602b3,128293,4000393
  //   ,729863,50313,fff00393,140006f,b55333,100393,5393b3,fff38393,737533,8067
  //   contents of _17_fib_rec (hex, n*v repeats v):
  //   40000113,500513,8000ef,c0001073,100293,a2c463,8067,fe810113,113023
  //   ,a13423,fff50513,fe5ff0ef,a13823,813503,ffe50513,fd5ff0ef,1013303
  //   ,650533,13083,1810113,8067
endmodule
